# Fritzing sketch schema_elettrico (saved by Fritzing 0.9.3b)
breadboards: 2

parts:
  MH-ET_LIVE_ESP32_DEVKIT1 = MH-ET LIVE ESP32 DEVKIT 38 pins
  S1 = Pushbutton [package="[THT]"]
  S2 = Pushbutton [package="[THT]"]
  S3 = Pushbutton [package="[THT]"]
  M1 = NEO-6M GPS Module [part_number=GY-GPS6MV2]
  OLED1 = OLED 128x64 I2C Monochrome Display

nets:
  N1: MH-ET_LIVE_ESP32_DEVKIT1.IO32, S1.Pin_3, S1.Pin_4
  N2: MH-ET_LIVE_ESP32_DEVKIT1.IO33, S2.Pin_3, S2.Pin_4
  N3: MH-ET_LIVE_ESP32_DEVKIT1.IO26, M1.Tx
  N4: MH-ET_LIVE_ESP32_DEVKIT1.IO27, M1.Rx
  N5: MH-ET_LIVE_ESP32_DEVKIT1.IO14, S3.Pin_3, S3.Pin_4
  GND: MH-ET_LIVE_ESP32_DEVKIT1.GND#58, S1.Pin_1, S1.Pin_2, S2.Pin_1, S2.Pin_2, S3.Pin_1, S3.Pin_2, M1.GND, OLED1.GND
  5V: MH-ET_LIVE_ESP32_DEVKIT1.5V, M1.Vcc, OLED1.VDD
  N6: MH-ET_LIVE_ESP32_DEVKIT1.IO22, OLED1.SDA
  N7: MH-ET_LIVE_ESP32_DEVKIT1.IO21, OLED1.SCK

custom parts:
  MH-ET LIVE ESP32 DEVKIT 38 pins: http://mh.nodebb.com/topic/2/mh-et-live-esp32-devkit
  NEO-6M GPS Module: GY-GPS6MV2 NEO-6M GPS Module Module based on U-blox NEO-6M GPS engine, incorporating regulator for 3.3-5V DC input, MS621FE-compatible rechargeable battery for backup and EEPROM for storing configuration settings. Links: NEO-6 series product information page NEO-6 Datasheet
